// Logisim project brainfuck.circ as structural Verilog: 5 circuits, main circuit main
module main (
);

  wire Clock_out, controll_section_1_data_minus, controll_section_1_data_plus, controll_section_1_halt,
       controll_section_1_iar_minus, controll_section_1_iar_plus, controll_section_1_in,
       controll_section_1_jp_minus, controll_section_1_jp_plus, controll_section_1_mar_minus,
       controll_section_1_mar_plus, controll_section_1_out, not_1_out, not_2_out, not_3_out, not_4_out,
       not_5_out, or_1_out, register_1_q, Reset_out;
  wire [6:0] bit_extender_1_out, keyboard_1_data;
  wire [7:0] bit_extender_2_out, IAR_always, incdecsection_1_output, JP_always, MAR_always,
       multiplexer_1_out, ram_1_data, rom_1_data;

  Clock Clock (.out(Clock_out));
  Controll_Section controll_section_1 (
    .clock(Clock_out), .JP(JP_always), .INS(rom_1_data), .MAR(MAR_always), .DATA(ram_1_data),
    .in(controll_section_1_in), .out(controll_section_1_out), .JP_plus(controll_section_1_jp_plus),
    .JP_minus(controll_section_1_jp_minus), .IAR_plus(controll_section_1_iar_plus),
    .IAR_minus(controll_section_1_iar_minus), .MAR_plus(controll_section_1_mar_plus),
    .MAR_minus(controll_section_1_mar_minus), .DATA_plus(controll_section_1_data_plus),
    .DATA_minus(controll_section_1_data_minus), .halt(controll_section_1_halt));
  Register #(.width(1)) register_1 (.D(1'b1), .en(or_1_out), .Q(register_1_q), .clk(Clock_out), .clr(Reset_out));
  buf or_1 (or_1_out, controll_section_1_halt);  // OR_Gate
  IncDecer JP (
    .INC(controll_section_1_jp_plus), .DEC(controll_section_1_jp_minus), .Enable(1'b0), .Set(1'b0),
    .Reset(Reset_out), .Clock(Clock_out), .\always (JP_always));  // open: Data, controlled
  IncDecer IAR (
    .INC(controll_section_1_iar_plus), .DEC(controll_section_1_iar_minus), .Enable(1'b0), .Set(1'b0),
    .Reset(Reset_out), .Clock(Clock_out), .\always (IAR_always));  // open: Data, controlled
  IncDecer MAR (
    .INC(controll_section_1_mar_plus), .DEC(controll_section_1_mar_minus), .Enable(1'b0), .Set(1'b0),
    .Reset(Reset_out), .Clock(Clock_out), .\always (MAR_always));  // open: Data, controlled
  // Probe on JP_always
  // Probe on IAR_always
  // Probe on MAR_always
  not not_1 (not_1_out, Clock_out);
  ROM rom_1 (.addr(IAR_always), .data(rom_1_data));  // open: sel
  RAM #(.bus("separate")) ram_1 (
    .addr(MAR_always), .din(multiplexer_1_out), .data(ram_1_data), .str(not_1_out), .clk(not_1_out),
    .clr(Reset_out));  // open: sel, ld
  Bit_Extender #(.out_width(7)) bit_extender_1 (.in(ram_1_data), .out(bit_extender_1_out));
  TTY tty_1 (.data(bit_extender_1_out), .clk(not_2_out), .we(controll_section_1_out), .clr(Reset_out));
  not not_2 (not_2_out, Clock_out);
  IncDecSection incdecsection_1 (
    .Inc(controll_section_1_data_plus), .Dec(controll_section_1_data_minus), .Input(ram_1_data),
    .Output(incdecsection_1_output));
  LED Running (.in(register_1_q));
  Keyboard keyboard_1 (.clk(not_4_out), .re(not_3_out), .data(keyboard_1_data));  // open: clr, avail
  not not_3 (not_3_out, register_1_q);
  not not_4 (not_4_out, controll_section_1_in);
  Button Reset (.out(Reset_out));
  assign bit_extender_2_out = {{1{1'b0}}, keyboard_1_data};  // Bit_Extender bit_extender_2
  Multiplexer #(.width(8), .enable("false")) multiplexer_1 (
    .in0(bit_extender_2_out), .in1(incdecsection_1_output), .out(multiplexer_1_out), .sel(not_5_out));
  not not_5 (not_5_out, controll_section_1_in);

  // Notes on the sheet:
  //   contents of rom_1 (hex, n*v repeats v):
  //   7*2 6 3 1 7*2 0 7 1 5 2 5 2 5
endmodule

// Controll\nSection
module Controll_Section (
  input  clock,
  input  [7:0] JP,
  input  [7:0] INS,
  input  [7:0] MAR,
  input  [7:0] DATA,
  output JP_plus,
  output JP_minus,
  output IAR_plus,
  output IAR_minus,
  output MAR_plus,
  output MAR_minus,
  output DATA_plus,
  output DATA_minus,
  output in,
  output out,
  output halt
);

  wire _0_out, _1_out, _2_out, _3_out, _4_out, _5_out, and_1_out, comparator_1_eq, comparator_2_eq,
       comparator_2_gt, comparator_2_lt, comparator_3_eq, comparator_4_eq, decoder_1_out0, decoder_1_out1,
       decoder_1_out2, decoder_1_out3, decoder_1_out4, decoder_1_out5, decoder_1_out6, decoder_1_out7,
       i_minus_out, i_plus_out, j_minus_out, j_plus_out, Path_Finder_out;
  wire [2:0] bit_extender_1_out;

  Comparator comparator_1 (.a(JP), .b({8{1'b1}}), .eq(comparator_1_eq));  // open: gt, lt
  Comparator comparator_2 (.a(JP), .b({8{1'b0}}), .gt(comparator_2_gt), .eq(comparator_2_eq), .lt(comparator_2_lt));
  Bit_Extender #(.out_width(3)) bit_extender_1 (.in(INS), .out(bit_extender_1_out));
  Decoder #(.select(3), .enable("false")) decoder_1 (
    .out0(decoder_1_out0), .out1(decoder_1_out1), .out2(decoder_1_out2), .out3(decoder_1_out3),
    .out4(decoder_1_out4), .out5(decoder_1_out5), .out6(decoder_1_out6), .out7(decoder_1_out7),
    .sel(bit_extender_1_out));
  Comparator comparator_3 (.a(MAR), .b({8{1'b0}}), .eq(comparator_3_eq));  // open: gt, lt
  Comparator comparator_4 (.a(DATA), .b({8{1'b0}}), .eq(comparator_4_eq));  // open: gt, lt
  // Probe on comparator_1_eq
  // Probe on comparator_2_gt
  // Probe on comparator_2_eq
  // Probe on comparator_2_lt
  // Probe on decoder_1_out7
  // Probe on decoder_1_out6
  // Probe on decoder_1_out5
  // Probe on decoder_1_out4
  // Probe on decoder_1_out3
  // Probe on decoder_1_out2
  // Probe on decoder_1_out1
  // Probe on decoder_1_out0
  // Probe on comparator_3_eq
  // Probe on comparator_4_eq
  // NOT_Gate Path_Finder has open pins: in=open, out=Path_Finder_out
  and and_1 (and_1_out, ~_0_out, ~_1_out, ~_2_out, ~_3_out);  // AND_Gate
  // Probe on clock
  and i_plus (i_plus_out, _4_out, comparator_2_gt);
  and i_minus (i_minus_out, _4_out, comparator_2_lt);
  and j_plus (j_plus_out, _4_out, decoder_1_out6);
  and j_minus (j_minus_out, _4_out, decoder_1_out7);
  and _0 (_0_out, clock, comparator_2_eq, comparator_4_eq, decoder_1_out6);
  and _1 (_1_out, clock, comparator_2_eq, ~comparator_4_eq, decoder_1_out6);  // AND_Gate
  and _2 (_2_out, clock, comparator_1_eq, decoder_1_out6);
  and _3 (_3_out, clock, comparator_2_eq, decoder_1_out7);
  and _4 (_4_out, clock, and_1_out, ~comparator_2_eq);  // AND_Gate
  and _5 (_5_out, clock, comparator_2_eq, decoder_1_out0);
  and and_2 (MAR_minus, _5_out, ~comparator_3_eq);  // AND_Gate
  and u_halt (halt, _5_out, comparator_3_eq);
  and _6 (MAR_plus, clock, comparator_2_eq, decoder_1_out1);
  and _7 (DATA_plus, clock, comparator_2_eq, decoder_1_out2);
  and _8 (DATA_minus, clock, comparator_2_eq, decoder_1_out3);
  and _9 (in, clock, comparator_2_eq, decoder_1_out4);
  and a (out, clock, comparator_2_eq, decoder_1_out5);
  or or_1 (JP_plus, _0_out, _2_out, j_plus_out, 1'b0);
  or or_2 (JP_minus, _3_out, j_minus_out, 1'b0);
  or or_3 (IAR_plus, _0_out, _1_out, i_plus_out, MAR_minus, MAR_plus, DATA_plus, DATA_minus, in, out);
  or or_4 (IAR_minus, _3_out, i_minus_out, 1'b0);
endmodule

// Inc\nDec\nReg
module IncDecer (
  input  INC,
  input  DEC,
  input  Enable,
  input  Set,
  input  [7:0] Data,
  input  Reset,
  input  Clock,
  output [7:0] \always ,
  output [7:0] controlled
);

  wire and_1_out, not_1_out;
  wire [1:0] controlled_buffer_1_out;

  and and_1 (and_1_out, ~INC, ~DEC, ~Enable, ~Set);  // AND_Gate
  assign controlled_buffer_1_out = INC ? 2'b01 : 2'bz;  // Controlled_Buffer controlled_buffer_1
  assign controlled_buffer_1_out = DEC ? 2'b11 : 2'bz;  // Controlled_Buffer controlled_buffer_2
  assign controlled_buffer_1_out = Set ? 2'b10 : 2'bz;  // Controlled_Buffer controlled_buffer_3
  assign controlled_buffer_1_out = and_1_out ? 2'b00 : 2'bz;  // Controlled_Buffer controlled_buffer_4
  not not_1 (not_1_out, Clock);
  Counter counter_1 (
    .load(controlled_buffer_1_out[1]), .D(Data), .count(controlled_buffer_1_out[0]), .Q(\always ),
    .clk(not_1_out), .clr(Reset));  // open: carry
  assign controlled = Enable ? \always  : 8'bz;  // Controlled_Buffer controlled_buffer_5
endmodule

// IncDec
module IncDecSection (
  input  Inc,
  input  Dec,
  input  [7:0] Input,
  output [7:0] Output
);

  wire and_1_out;
  wire [7:0] controlled_buffer_1_out;

  and and_1 (and_1_out, ~Dec, ~Inc);  // AND_Gate
  assign controlled_buffer_1_out = Dec ? {8{1'b1}} : 8'bz;  // Controlled_Buffer controlled_buffer_1
  assign controlled_buffer_1_out = and_1_out ? {8{1'b0}} : 8'bz;  // Controlled_Buffer controlled_buffer_2
  assign controlled_buffer_1_out = Inc ? 8'h1 : 8'bz;  // Controlled_Buffer controlled_buffer_3
  Adder adder_1 (.a(controlled_buffer_1_out), .b(Input), .out(Output));  // open: cin, cout
endmodule

module Delayer (
  input  \input ,
  input  clock,
  output \output 
);

  wire not_1_out;

  Register #(.width(1)) register_1 (.D(\input ), .Q(\output ), .clk(not_1_out));  // open: en, clr
  not not_1 (not_1_out, clock);
endmodule
